# Fritzing sketch wire_diagram_3 (saved by Fritzing 1.0.5)
breadboards: 1

parts:
  Bauteil1 = RGB Color Sensor - TCA3472
  Grove1 = Grove OLED 128x96
  Bauteil2 = Adafruit PCA9685 PWM/Servo Breakout [part_number=815]
  Power_plug1 = Power plug
  J1 = Basic Servo
  J2 = Basic Servo
  TI_MSP-EXP430FR1 = MSP-EXP430FR2355
  C1 = Electrolytic Capacitor [package="2cm H-Type"]

nets:
  N1: Bauteil1.LED, TI_MSP-EXP430FR1.P1.7
  N2: Bauteil1.SDA, Grove1.SDA, Bauteil2.SDA, TI_MSP-EXP430FR1.P1.2
  N3: Bauteil1.SCL, Grove1.SCL, Bauteil2.SCL, TI_MSP-EXP430FR1.P1.3
  VCC: Bauteil1.3V3, Grove1.VCC, Bauteil2.VCC, TI_MSP-EXP430FR1.3.3V
  GND: Bauteil1.GND, Grove1.GND, Bauteil2.GND, Power_plug1.GND, J1.gnd, J2.gnd, TI_MSP-EXP430FR1.GND, C1.-
  VCC_2: Bauteil2.5.0V, J1.vcc, J2.vcc, C1.+
  N4: Bauteil2.PWRIN, Power_plug1.VCC
  N5: Bauteil2.PWM0, J1.pulse
  N6: Bauteil2.PWM8, J2.pulse

custom parts:
  Adafruit PCA9685 PWM/Servo Breakout: Using only two pins, control 16 free-running PWM outputs! I2C-controlled PWM driver with a built in clock. Unlike the TLC5940 family, you do not need to continuously send it signal tying up your microcontroller, its completely free running! 5V compliant, which means you can control it from a 3.3V microcontroller and still safely drive up to 6V outputs (this is good for when you want to control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
  Power plug: power plug
  MSP-EXP430FR2355: Texas Instruments MSP430FR2355 LaunchPad
